# Fritzing sketch lab_1 (saved by Fritzing 0.8.7b)
breadboards: 1

parts:
  Part1 = Arduino Uno (Rev3)
  R2 = Resistor [tolerance=±5% resistance=560 package=THT]
  S1 = Pushbutton [package="[THT]"]
  R3 = Resistor [tolerance=±5% resistance=560 package=THT]
  LED3 = LED - 5mm [color="Red (633nm)" package="5 mm [THT]"]
  LED2 = LED - 5mm [color="Red (633nm)" package="5 mm [THT]"]
  R1 = Resistor [tolerance=±5% resistance=560 package=THT]

nets:
  N1: Part1.D3_PWM, Part1.5V, S1.Pin_3, S1.Pin_4, R3.Pin_0, R3.Pin_1
  N2: Part1.D4, LED2.cathode
  N3: Part1.D5_PWM, LED3.cathode
  N4: Part1.GND, R2.Pin_1, R1.Pin_1
  N5: R2.Pin_0, LED3.anode
  N6: S1.Pin_1, S1.Pin_2
  N7: LED2.anode, R1.Pin_0
