# Fritzing sketch lab_2 (saved by Fritzing 0.9.2b)
breadboards: 1

parts:
  Part1 = Arduino Uno (Rev3)
  R2 = Resistor [tolerance=±5% resistance=560 package=THT]
  S1 = Pushbutton [package="[THT]"]
  R3 = Resistor [tolerance=±5% resistance=560 package=THT]
  LED3 = LED - 5mm [color="Red (633nm)" package="5 mm [THT]"]
  J1 = Piezo Speaker

nets:
  N1: Part1.D3_PWM, Part1.5V, S1.Pin_3, S1.Pin_4, R3.Pin_0, R3.Pin_1
  N2: Part1.D4, LED3.cathode
  N3: Part1.D5_PWM, J1.pin1
  N4: Part1.GND, R2.Pin_1, J1.pin2
  N5: R2.Pin_0, LED3.anode
  N6: S1.Pin_1, S1.Pin_2
