# Fritzing sketch lab_3 (saved by Fritzing 0.8.7b)
breadboards: 1

parts:
  Part1 = Arduino Uno (Rev3)
  R2 = Resistor [tolerance=±5% resistance=560 package=THT]
  LED3 = LED - 5mm [color="Red (633nm)" package="5 mm [THT]"]
  J1 = Piezo Speaker
  R4 = Rotary Potentiometer (Small) [maximum_resistance=100kΩ package=THT]
  S3 = Pushbutton [package="[THT]"]
  S4 = Pushbutton [package="[THT]"]
  R7 = Resistor [tolerance=±5% resistance=560 package=THT]
  R8 = Resistor [tolerance=±5% resistance=560 package=THT]

nets:
  N1: Part1.A0, R4.wiper
  N2: Part1.D2, S4.Pin_1, S4.Pin_2, R7.Pin_0
  N3: Part1.D3_PWM, S3.Pin_1, S3.Pin_2, R8.Pin_0
  N4: Part1.D4, LED3.cathode
  N5: Part1.D5_PWM, J1.pin1
  N6: Part1.5V, R4.leg1, S3.Pin_3, S3.Pin_4, S4.Pin_3, S4.Pin_4
  N7: Part1.GND, R2.Pin_1, J1.pin2, R4.leg2, R7.Pin_1, R8.Pin_1
  N8: R2.Pin_0, LED3.anode
