# Fritzing sketch lab_5 (saved by Fritzing 0.8.7b)
breadboards: 1

parts:
  Part1 = Arduino Uno (Rev3)
  R2 = Resistor [tolerance=±5% resistance=560 package=THT]
  LED3 = LED - 5mm [color="Red (633nm)" package="5 mm [THT]"]
  S6 = Pushbutton [package="[THT]"]
  LED4 = LED - 5mm [color="Red (633nm)" package="5 mm [THT]"]
  R10 = Resistor [tolerance=±5% resistance=560 package=THT]
  S7 = Pushbutton [package="[THT]"]
  LED5 = RGB LED (com. anode, rbg) [package="5 mm [THT]"]
  R12 = Resistor [tolerance=±5% resistance=560 package=THT]
  R13 = Resistor [tolerance=±5% resistance=560 package=THT]
  R14 = Resistor [tolerance=±5% resistance=560 package=THT]
  R15 = Resistor [tolerance=±5% resistance=560 package=THT]
  R16 = Resistor [tolerance=±5% resistance=560 package=THT]

nets:
  N1: Part1.D8, R12.Pin_0
  N2: Part1.D2, S6.Pin_1, S6.Pin_2, R16.Pin_0
  N3: Part1.D3_PWM, S7.Pin_1, S7.Pin_2, R15.Pin_0
  N4: Part1.D4, LED4.cathode
  N5: Part1.D5_PWM, LED3.cathode
  N6: Part1.D6_PWM, R14.Pin_0
  N7: Part1.D7, R13.Pin_0
  N8: Part1.5V, S6.Pin_3, S6.Pin_4, LED5.common_anode
  N9: Part1.GND, R2.Pin_1, R10.Pin_1, R15.Pin_1, R16.Pin_1
  N10: R2.Pin_0, LED3.anode
  N11: LED4.anode, R10.Pin_0
  N12: S7.Pin_3, S7.Pin_4
  N13: LED5.red_cathode, R12.Pin_1
  N14: LED5.blue_cathode, R13.Pin_1
  N15: LED5.green_cathode, R14.Pin_1
