# Fritzing sketch lab_7 (saved by Fritzing 0.9.2b)
breadboards: 1

parts:
  LED5 = RGB LED (com. anode, rbg) [package="5 mm [THT]"]
  R12 = Resistor [tolerance=±5% resistance=560 package=THT]
  R13 = Resistor [tolerance=±5% resistance=560 package=THT]
  U1 = TMP36 [package=to-92-kit]
  DFRobot_LCD_keypad_shield1 = LCD keypad Shield  # not connected
  Part1 = Arduino Uno (Rev3)

nets:
  N1: LED5.red_cathode, R12.Pin_1
  VCC: LED5.common_anode, U1.VCC, Part1.5V
  N2: LED5.blue_cathode, R13.Pin_1
  N3: R12.Pin_0, Part1.D10_PWM/SS
  N4: R13.Pin_0, Part1.D9_PWM
  N5: U1.VOUT, Part1.A1
  GND: U1.GND, Part1.GND

custom parts:
  LCD keypad Shield: A 2 row LCD shield with buttons, and contrast regulator.
