# Fritzing sketch lab_7_shield (saved by Fritzing 0.9.2b)
breadboards: 1

parts:
  LED5 = RGB LED (com. anode, rbg) [package="5 mm [THT]"]
  R12 = Resistor [tolerance=±5% resistance=560 package=THT]
  R13 = Resistor [tolerance=±5% resistance=560 package=THT]
  U1 = TMP36 [package=to-92-kit]
  DFRobot_LCD_keypad_shield1 = LCD keypad Shield

nets:
  N1: LED5.red_cathode, R12.Pin_1
  N2: LED5.common_anode, U1.VCC
  N3: LED5.blue_cathode, R13.Pin_1
  N4: R12.Pin_0, DFRobot_LCD_keypad_shield1.D11
  N5: R13.Pin_0, DFRobot_LCD_keypad_shield1.D3
  N6: U1.VOUT, DFRobot_LCD_keypad_shield1.A1

custom parts:
  LCD keypad Shield: A 2 row LCD shield with buttons, and contrast regulator.
