# Fritzing sketch lab_8 (saved by Fritzing 0.9.2b)
breadboards: 1

parts:
  Part1 = Arduino Uno (Rev3)
  J1 = Piezo Speaker
  LED5 = LED - 5mm [color="Red (633nm)" package="5 mm [THT]"]
  R11 = Resistor [tolerance=±5% resistance=560 package=THT]
  LED6 = LED - 5mm [color="Green (555nm)" package="5 mm [THT]"]
  R12 = Resistor [tolerance=±5% resistance=560 package=THT]

nets:
  N1: Part1.D11_PWM/MOSI, J1.pin1
  N2: Part1.D12/MISO, LED5.cathode
  N3: Part1.D13/SCK, LED6.cathode
  N4: Part1.GND, J1.pin2, R11.Pin_1, R12.Pin_1
  N5: LED5.anode, R11.Pin_0
  N6: LED6.anode, R12.Pin_0
