# Fritzing sketch lab_8.shield (saved by Fritzing 0.9.2b)
breadboards: 1

parts:
  J1 = Piezo Speaker
  LED5 = LED - 5mm [color="Red (633nm)" package="5 mm [THT]"]
  R11 = Resistor [tolerance=±5% resistance=560 package=THT]
  LED6 = LED - 5mm [color="Green (555nm)" package="5 mm [THT]"]
  R12 = Resistor [tolerance=±5% resistance=560 package=THT]
  DFRobot_LCD_keypad_shield1 = LCD keypad Shield

nets:
  N1: J1.pin1, DFRobot_LCD_keypad_shield1.D3
  N2: J1.pin2, R11.Pin_1, R12.Pin_1
  N3: LED5.cathode, DFRobot_LCD_keypad_shield1.D11
  N4: LED5.anode, R11.Pin_0
  N5: LED6.cathode, DFRobot_LCD_keypad_shield1.D12
  N6: LED6.anode, R12.Pin_0

custom parts:
  LCD keypad Shield: A 2 row LCD shield with buttons, and contrast regulator.
